# Fritzing sketch 7Seg4Dig Clock (saved by Fritzing 0.9.3b)
breadboards: 1

parts:
  R9 = Resistor [tolerance=±5% resistance=1k package="0603 [SMD]"]
  R10 = Resistor [tolerance=±5% resistance=1k package="0603 [SMD]"]
  R11 = Resistor [tolerance=±5% resistance=1k package="0603 [SMD]"]
  R12 = Resistor [tolerance=±5% resistance=1k package="0603 [SMD]"]
  R13 = Resistor [tolerance=±5% resistance=1k package="0603 [SMD]"]
  R14 = Resistor [tolerance=±5% resistance=1k package="0603 [SMD]"]
  R15 = Resistor [tolerance=±5% resistance=1k package="0603 [SMD]"]
  R16 = Resistor [tolerance=±5% resistance=1k package="0603 [SMD]"]
  LED2 = 7-SEGMENT-4DIGIT-YOUNGSUN [package=7-segment-4digit-youngsun-longpads]
  Componente1 = Arduino Uno (Rev3)
  Tiny_RTC2 = Tiny RTC

nets:
  N1: R9.Pin_0, Componente1.D4
  N2: R9.Pin_1, LED2.COL-A
  N3: R10.Pin_0, Componente1.D2
  N4: R10.Pin_1, LED2.F
  N5: R11.Pin_0, Componente1.D3_PWM
  N6: R11.Pin_1, LED2.DP
  N7: R12.Pin_0, Componente1.D9_PWM
  N8: R12.Pin_1, LED2.D
  N9: R13.Pin_0, Componente1.D6_PWM
  N10: R13.Pin_1, LED2.DIG1
  N11: R14.Pin_0, Componente1.D8
  N12: R14.Pin_1, LED2.E
  N13: R15.Pin_0, Componente1.D5_PWM
  N14: R15.Pin_1, LED2.DIG2
  N15: R16.Pin_0, Componente1.D7
  N16: R16.Pin_1, LED2.APOS-A
  N17: LED2.DIG3, Componente1.A3
  N18: LED2.DIG4, Componente1.A2
  N19: LED2.APOS-C, Componente1.A1
  N20: LED2.COL-C, Componente1.A0
  5V: LED2.C, LED2.A, LED2.G, LED2.B, Componente1.5V, Tiny_RTC2.VCC
  N21: Componente1.A4/SDA, Tiny_RTC2.SDA
  N22: Componente1.A5/SCL, Tiny_RTC2.SCL
  GND: Componente1.GND, Tiny_RTC2.GND

custom parts:
  Tiny RTC: Tiny RTC I2C module DS1370Z RTC and AT24C32 EEPROM
